# Fritzing sketch SbusRx2Joystick (saved by Fritzing 0.9.4)
circuit board: 8.46667cm x 5.64444cm
breadboards: 1

parts:
  Pro_Micro1 = SparkFun Pro Micro
  R1 = Resistor [tolerance=±5% resistance=10k package=THT]
  R2 = Resistor [tolerance=±5% resistance=4.7k package=THT]
  Q1 = NPN-Transistor [package="TO92 [THT]"]
  Receiver1 = Futaba R7008SB

nets:
  N1: Pro_Micro1.RX1, R1.Pin_1, Q1.C
  N2: Pro_Micro1.GND, Q1.E, Receiver1.SBUS-
  N3: Pro_Micro1.3, Pro_Micro1.4
  N4: Pro_Micro1.VCC, R1.Pin_0, Receiver1.SBUS+
  N5: R2.Pin_0, Receiver1.SBUSS
  N6: R2.Pin_1, Q1.B

custom parts:
  SparkFun Pro Micro: The Pro Micro is similar to the Pro Mini except with an ATmega32U4 on board. The USB transceiver inside the 32U4 allows us to add USB connectivity on-board and do away with bulky external USB interface. Based on: https://github.com/unorthodox-engineers/unorthodox-arduino/blob/master/Unorthodox/fritzing/parts/Pro%20Micro.fzpz
  Futaba R7008SB: Futaba Corporation R7008SB FASSTest Telemetry Receiver
